// Logisim project P3_Logisim_CPU.circ as structural Verilog: 9 circuits, main circuit main
module main (
  input  in_1,
  output [31:0] out_2,
  output [31:0] out_3,
  output out_4,
  output [4:0] out_5,
  output [31:0] out_6,
  output out_7,
  output [31:0] out_8,
  output [31:0] out_9
);

  wire and_1_out, clk, controller_1_alusrc, controller_1_memtoreg, controller_1_regdst, nPC_sel;
  wire [1:0] controller_1_extop;
  wire [2:0] controller_1_aluop;
  wire [31:0] adder_1_out, adder_2_out, dm_1_rd, ext_1_out, grf_1_rd1, multiplexer_2_out, multiplexer_3_out;

  IFU ifu_1 (.PC(multiplexer_3_out), .clk(clk), .reset(in_1), .Instr(out_2), .pc_2(out_3));
  Controller controller_1 (
    .op(out_2[31:26]), .func(out_2[5:0]), .MemWrite(out_7), .RegWrite(out_4), .EXTop(controller_1_extop),
    .ALUSrc(controller_1_alusrc), .RegDst(controller_1_regdst), .MemtoReg(controller_1_memtoreg),
    .nPC_sel(nPC_sel), .ALUop(controller_1_aluop));  // open: EXTuse
  Multiplexer #(.width(5)) multiplexer_1 (
    .in0(out_2[15:11]), .in1(out_2[20:16]), .out(out_5), .sel(controller_1_regdst));  // open: en
  GRF grf_1 (
    .A1(out_2[25:21]), .A2(out_2[20:16]), .A3(out_5), .WD(out_6), .clk(clk), .reset(in_1), .WE(out_4),
    .RD1(grf_1_rd1), .RD2(out_9));
  Multiplexer #(.width(32)) multiplexer_2 (
    .in0(out_9), .in1(ext_1_out), .out(multiplexer_2_out), .sel(controller_1_alusrc));  // open: en
  ALU alu_1 (.num1(grf_1_rd1), .num2(multiplexer_2_out), .ALUop({1'b0, controller_1_aluop}), .ans(out_8));
  Adder #(.width(32)) adder_1 (.a(out_3), .b(32'h4), .out(adder_1_out));  // open: cin, cout
  EXT ext_1 (.in(out_2[15:0]), .EXTop(controller_1_extop), .out(ext_1_out));
  Adder #(.width(32)) adder_2 (.a(adder_1_out), .b(ext_1_out), .out(adder_2_out));  // open: cin, cout
  DM dm_1 (.addr(out_8), .WD(out_9), .WE(out_7), .clk(clk), .reset(in_1), .RD(dm_1_rd));
  Multiplexer #(.width(32)) multiplexer_3 (
    .in0(adder_1_out), .in1(adder_2_out), .out(multiplexer_3_out), .sel(and_1_out));  // open: en
  and and_1 (and_1_out, out_8[0], nPC_sel);
  Multiplexer #(.width(32)) multiplexer_4 (
    .in0(out_8), .in1(dm_1_rd), .out(out_6), .sel(controller_1_memtoreg));  // open: en
  Clock clock_1 (.out(clk));

  // Other names for the same wires on the sheet: func[5:0] = out_2[5:0]; Instr[31:0] = out_2;
  //   offset_immediate[15:0] = out_2[15:0]; shamt[4:0] = out_2[10:6]; rd[4:0] = out_2[15:11]; rt[4:0] = out_2[20:16];
  //   rs[4:0] = out_2[25:21]; op[5:0] = out_2[31:26]; MemAddr[31:0] = out_8; MemData[31:0] = out_9; MemWrite = out_7;
  //   pc[31:0] = out_3; RegAddr[4:0] = out_5; GRF_WD[31:0] = out_6; RegData[31:0] = out_6; RegWrite = out_4;
  //   reset = in_1
endmodule

module IFU (
  input  [31:0] PC,
  input  clk,
  input  reset,
  output [31:0] Instr,
  output [31:0] pc_2
);

  wire [31:0] PC_0x3000_q, subtractor_1_out;

  Subtractor #(.width(32)) subtractor_1 (.a(PC), .b(32'h3000), .out(subtractor_1_out));  // open: bin, bout
  Register #(.width(32)) PC_0x3000 (.D(subtractor_1_out), .Q(PC_0x3000_q), .clk(clk), .clr(reset));  // open: en
  Adder #(.width(32)) adder_1 (.a(PC_0x3000_q), .b(32'h3000), .out(pc_2));  // open: cin, cout
  ROM #(.addrWidth(12), .dataWidth(32)) rom_1 (.addr(PC_0x3000_q[13:2]), .data(Instr));  // open: sel

  // Notes on the sheet:
  //   contents of rom_1 (hex, n*v repeats v):
  //   10a4020 10a4020 10a4020
endmodule

module GRF (
  input  clk,
  input  reset,
  input  WE,
  input  [4:0] A1,
  input  [4:0] A2,
  input  [4:0] A3,
  input  [31:0] WD,
  output [31:0] RD1,
  output [31:0] RD2
);

  wire [31:0] demultiplexer_1_out1, demultiplexer_1_out2, demultiplexer_1_out3, demultiplexer_1_out4,
       demultiplexer_1_out5, demultiplexer_1_out6, demultiplexer_1_out7, demultiplexer_1_out8,
       demultiplexer_1_out9, demultiplexer_1_out10, demultiplexer_1_out11, demultiplexer_1_out12,
       demultiplexer_1_out13, demultiplexer_1_out14, demultiplexer_1_out15, demultiplexer_1_out16,
       demultiplexer_1_out17, demultiplexer_1_out18, demultiplexer_1_out19, demultiplexer_1_out20,
       demultiplexer_1_out21, demultiplexer_1_out22, demultiplexer_1_out23, demultiplexer_1_out24,
       demultiplexer_1_out25, demultiplexer_1_out26, demultiplexer_1_out27, demultiplexer_1_out28,
       demultiplexer_1_out29, demultiplexer_1_out30, demultiplexer_1_out31, O0, O1, O2, O3, O4, O5, O6, O7,
       O8, O9, O10, O11, O12, O13, O14, O15, O16, O17, O18, O19, O20, O21, O22, O23, O24, O25, O26, O27, O28,
       O29, O30, O31;

  Demultiplexer #(.select(5), .width(32), .tristate("true")) demultiplexer_1 (
    .out1(demultiplexer_1_out1), .out2(demultiplexer_1_out2), .out3(demultiplexer_1_out3),
    .out4(demultiplexer_1_out4), .out5(demultiplexer_1_out5), .out6(demultiplexer_1_out6),
    .out7(demultiplexer_1_out7), .out8(demultiplexer_1_out8), .out9(demultiplexer_1_out9),
    .out10(demultiplexer_1_out10), .out11(demultiplexer_1_out11), .out12(demultiplexer_1_out12),
    .out13(demultiplexer_1_out13), .out14(demultiplexer_1_out14), .out15(demultiplexer_1_out15),
    .out16(demultiplexer_1_out16), .out17(demultiplexer_1_out17), .out18(demultiplexer_1_out18),
    .out19(demultiplexer_1_out19), .out20(demultiplexer_1_out20), .out21(demultiplexer_1_out21),
    .out22(demultiplexer_1_out22), .out23(demultiplexer_1_out23), .out24(demultiplexer_1_out24),
    .out25(demultiplexer_1_out25), .out26(demultiplexer_1_out26), .out27(demultiplexer_1_out27),
    .out28(demultiplexer_1_out28), .out29(demultiplexer_1_out29), .out30(demultiplexer_1_out30),
    .out31(demultiplexer_1_out31), .in(WD), .sel(A3), .en(WE));  // open: out0
  Register #(.width(32)) register_1 (.D(demultiplexer_1_out16), .en(WE), .Q(O16), .clk(clk), .clr(reset));
  Register #(.width(32)) register_2 (.D(demultiplexer_1_out17), .en(WE), .Q(O17), .clk(clk), .clr(reset));
  Register #(.width(32)) register_3 (.D(demultiplexer_1_out18), .en(WE), .Q(O18), .clk(clk), .clr(reset));
  Register #(.width(32)) register_4 (.D(demultiplexer_1_out19), .en(WE), .Q(O19), .clk(clk), .clr(reset));
  Register #(.width(32)) register_5 (.D(demultiplexer_1_out20), .en(WE), .Q(O20), .clk(clk), .clr(reset));
  Register #(.width(32)) register_6 (.D(demultiplexer_1_out21), .en(WE), .Q(O21), .clk(clk), .clr(reset));
  Register #(.width(32)) register_7 (.D(demultiplexer_1_out22), .en(WE), .Q(O22), .clk(clk), .clr(reset));
  Register #(.width(32)) register_8 (.D(demultiplexer_1_out23), .en(WE), .Q(O23), .clk(clk), .clr(reset));
  Register #(.width(32)) register_9 (.D(demultiplexer_1_out24), .en(WE), .Q(O24), .clk(clk), .clr(reset));
  Register #(.width(32)) register_10 (.D(demultiplexer_1_out25), .en(WE), .Q(O25), .clk(clk), .clr(reset));
  Register #(.width(32)) register_11 (.D(demultiplexer_1_out26), .en(WE), .Q(O26), .clk(clk), .clr(reset));
  Register #(.width(32)) register_12 (.D(demultiplexer_1_out27), .en(WE), .Q(O27), .clk(clk), .clr(reset));
  Register #(.width(32)) register_13 (.D(demultiplexer_1_out28), .en(WE), .Q(O28), .clk(clk), .clr(reset));
  Register #(.width(32)) register_14 (.D(demultiplexer_1_out29), .en(WE), .Q(O29), .clk(clk), .clr(reset));
  Register #(.width(32)) register_15 (.D(demultiplexer_1_out30), .en(WE), .Q(O30), .clk(clk), .clr(reset));
  Register #(.width(32)) register_16 (.D(demultiplexer_1_out31), .en(WE), .Q(O31), .clk(clk), .clr(reset));
  Register #(.width(32)) register_17 (.en(WE), .Q(O0), .clk(clk), .clr(reset));  // open: D
  Register #(.width(32)) register_18 (.D(demultiplexer_1_out1), .en(WE), .Q(O1), .clk(clk), .clr(reset));
  Register #(.width(32)) register_19 (.D(demultiplexer_1_out2), .en(WE), .Q(O2), .clk(clk), .clr(reset));
  Register #(.width(32)) register_20 (.D(demultiplexer_1_out3), .en(WE), .Q(O3), .clk(clk), .clr(reset));
  Register #(.width(32)) register_21 (.D(demultiplexer_1_out4), .en(WE), .Q(O4), .clk(clk), .clr(reset));
  Register #(.width(32)) register_22 (.D(demultiplexer_1_out5), .en(WE), .Q(O5), .clk(clk), .clr(reset));
  Register #(.width(32)) register_23 (.D(demultiplexer_1_out6), .en(WE), .Q(O6), .clk(clk), .clr(reset));
  Register #(.width(32)) register_24 (.D(demultiplexer_1_out7), .en(WE), .Q(O7), .clk(clk), .clr(reset));
  Register #(.width(32)) register_25 (.D(demultiplexer_1_out8), .en(WE), .Q(O8), .clk(clk), .clr(reset));
  Register #(.width(32)) register_26 (.D(demultiplexer_1_out9), .en(WE), .Q(O9), .clk(clk), .clr(reset));
  Register #(.width(32)) register_27 (.D(demultiplexer_1_out10), .en(WE), .Q(O10), .clk(clk), .clr(reset));
  Register #(.width(32)) register_28 (.D(demultiplexer_1_out11), .en(WE), .Q(O11), .clk(clk), .clr(reset));
  Register #(.width(32)) register_29 (.D(demultiplexer_1_out12), .en(WE), .Q(O12), .clk(clk), .clr(reset));
  Register #(.width(32)) register_30 (.D(demultiplexer_1_out13), .en(WE), .Q(O13), .clk(clk), .clr(reset));
  Register #(.width(32)) register_31 (.D(demultiplexer_1_out14), .en(WE), .Q(O14), .clk(clk), .clr(reset));
  Register #(.width(32)) register_32 (.D(demultiplexer_1_out15), .en(WE), .Q(O15), .clk(clk), .clr(reset));
  Multiplexer #(.select(5), .width(32)) multiplexer_1 (
    .in0(O0), .in1(O1), .in2(O2), .in3(O3), .in4(O4), .in5(O5), .in6(O6), .in7(O7), .in8(O8), .in9(O9),
    .in10(O10), .in11(O11), .in12(O12), .in13(O13), .in14(O14), .in15(O15), .in16(O16), .in17(O17),
    .in18(O18), .in19(O19), .in20(O20), .in21(O21), .in22(O22), .in23(O23), .in24(O24), .in25(O25),
    .in26(O26), .in27(O27), .in28(O28), .in29(O29), .in30(O30), .in31(O31), .out(RD1), .sel(A1));  // open: en
  Multiplexer #(.select(5), .width(32)) multiplexer_2 (
    .in0(O0), .in1(O1), .in2(O2), .in3(O3), .in4(O4), .in5(O5), .in6(O6), .in7(O7), .in8(O8), .in9(O9),
    .in10(O10), .in11(O11), .in12(O12), .in13(O13), .in14(O14), .in15(O15), .in16(O16), .in17(O17),
    .in18(O18), .in19(O19), .in20(O20), .in21(O21), .in22(O22), .in23(O23), .in24(O24), .in25(O25),
    .in26(O26), .in27(O27), .in28(O28), .in29(O29), .in30(O30), .in31(O31), .out(RD2), .sel(A2));  // open: en
endmodule

module ALU (
  input  [31:0] num1,
  input  [31:0] num2,
  input  [3:0] ALUop,
  output [31:0] ans
);

  wire [0:0] comparator_1_eq, comparator_1_gt, comparator_1_lt;
  wire [31:0] adder_1_out, or_1_out, subtractor_1_out;

  Subtractor #(.width(32)) subtractor_1 (.a(num1), .b(num2), .out(subtractor_1_out));  // open: bin, bout
  Adder #(.width(32)) adder_1 (.a(num1), .b(num2), .out(adder_1_out));  // open: cin, cout
  Comparator #(.width(32)) comparator_1 (
    .a(num1), .b(num2), .gt(comparator_1_gt[0]), .eq(comparator_1_eq[0]), .lt(comparator_1_lt[0]));
  assign or_1_out = num1 | num2;  // OR_Gate or_1, 32 bits wide
  Multiplexer #(.select(4), .width(32)) multiplexer_1 (
    .in0(adder_1_out), .in1(subtractor_1_out), .in2(or_1_out), .in3({{31{1'b0}}, comparator_1_gt[0]}),
    .in4({{31{1'b0}}, comparator_1_eq[0]}), .in5({{31{1'b0}}, comparator_1_lt[0]}), .out(ans), .sel(ALUop));  // open: in6, in7, in8, in9, in10, in11, in12, in13, in14, in15, en
endmodule

module DM (
  input  [31:0] addr,
  input  [31:0] WD,
  input  WE,
  input  clk,
  input  reset,
  output [31:0] RD
);

  wire not_1_out;

  not not_1 (not_1_out, WE);
  RAM #(.addrWidth(12), .dataWidth(32), .bus("separate")) ram_1 (
    .addr(addr[13:2]), .din(WD), .data(RD), .str(WE), .clk(clk), .ld(not_1_out), .clr(reset));  // open: sel
endmodule

module EXT (
  input  [15:0] in,
  input  [1:0] EXTop,
  output [31:0] out
);

  wire [29:0] bit_extender_3_out;
  wire [31:0] bit_extender_1_out, bit_extender_2_out;

  assign bit_extender_1_out = {{16{in[15]}}, in};  // Bit_Extender bit_extender_1
  assign bit_extender_2_out = {{16{1'b0}}, in};  // Bit_Extender bit_extender_2
  assign bit_extender_3_out = {{14{in[15]}}, in};  // Bit_Extender bit_extender_3
  Multiplexer #(.select(2), .width(32)) multiplexer_1 (
    .in0(bit_extender_1_out), .in1(bit_extender_2_out), .in2({in, {16{1'b0}}}),
    .in3({bit_extender_3_out, 2'b00}), .out(out), .sel(EXTop));  // open: en
endmodule

module Controller (
  input  [5:0] op,
  input  [5:0] func,
  output MemWrite,
  output RegWrite,
  output [1:0] EXTop,
  output ALUSrc,
  output RegDst,
  output MemtoReg,
  output nPC_sel,
  output [2:0] ALUop,
  output EXTuse
);

  wire and_logic_1_add, and_logic_1_beq, and_logic_1_lui, and_logic_1_lw, and_logic_1_ori, and_logic_1_sub,
       and_logic_1_sw;

  AND_Logic and_logic_1 (
    .op0(op[0]), .op1(op[1]), .op2(op[2]), .op3(op[3]), .op4(op[4]), .op5(op[5]), .func0(func[0]),
    .func1(func[1]), .func2(func[2]), .func3(func[3]), .func4(func[4]), .func5(func[5]),
    .add(and_logic_1_add), .sub(and_logic_1_sub), .ori(and_logic_1_ori), .lw(and_logic_1_lw),
    .sw(and_logic_1_sw), .beq(and_logic_1_beq), .lui(and_logic_1_lui));
  OR_Logic or_logic_1 (
    .add(and_logic_1_add), .sub(and_logic_1_sub), .ori(and_logic_1_ori), .lw(and_logic_1_lw),
    .sw(and_logic_1_sw), .beq(and_logic_1_beq), .lui(and_logic_1_lui), .MemWrite(MemWrite),
    .RegWrite(RegWrite), .EXTop0(EXTop[0]), .EXTop1(EXTop[1]), .ALUSrc(ALUSrc), .RegDst(RegDst),
    .MemtoReg(MemtoReg), .nPC_sel(nPC_sel), .ALUop0(ALUop[0]), .ALUop1(ALUop[1]), .ALUop2(ALUop[2]),
    .EXTuse(EXTuse));
endmodule

module AND_Logic (
  input  op0,
  input  op1,
  input  op2,
  input  op3,
  input  op4,
  input  op5,
  input  func0,
  input  func1,
  input  func2,
  input  func3,
  input  func4,
  input  func5,
  output add,
  output sub,
  output ori,
  output lw,
  output sw,
  output beq,
  output lui
);

  wire not_1_out, not_2_out, not_3_out, not_4_out, not_5_out, not_6_out, not_7_out, not_8_out, not_9_out,
       not_10_out, not_11_out, not_12_out, special;

  not not_1 (not_1_out, op0);
  not not_2 (not_2_out, op1);
  not not_3 (not_3_out, op2);
  not not_4 (not_4_out, op3);
  not not_5 (not_5_out, op4);
  not not_6 (not_6_out, op5);
  not not_7 (not_7_out, func0);
  not not_8 (not_8_out, func1);
  not not_9 (not_9_out, func2);
  not not_10 (not_10_out, func3);
  not not_11 (not_11_out, func4);
  not not_12 (not_12_out, func5);
  and u_add (add, func5, not_11_out, not_10_out, special, not_9_out, not_8_out, not_7_out);
  and u_sub (sub, func5, not_11_out, not_10_out, special, not_9_out, func1, not_7_out);
  and u_ori (ori, not_6_out, not_5_out, op3, op2, not_2_out, op0);
  and and_1 (special, not_1_out, not_2_out, not_3_out, not_4_out, not_5_out, not_6_out);
  and u_lw (lw, op5, not_5_out, not_4_out, not_3_out, op1, op0);
  and u_sw (sw, op5, not_5_out, op3, not_3_out, op1, op0);
  and u_beq (beq, not_6_out, not_5_out, not_4_out, op2, not_2_out, not_1_out);
  and u_lui (lui, not_6_out, not_5_out, op3, op2, op1, op0);
endmodule

module OR_Logic (
  input  add,
  input  sub,
  input  ori,
  input  lw,
  input  sw,
  input  beq,
  input  lui,
  output MemWrite,
  output RegWrite,
  output EXTop0,
  output EXTop1,
  output ALUSrc,
  output RegDst,
  output MemtoReg,
  output nPC_sel,
  output ALUop0,
  output ALUop1,
  output ALUop2,
  output EXTuse
);

  buf or_1 (MemWrite, sw);  // OR_Gate
  or or_2 (RegWrite, add, sub, ori, lw, lui);
  or or_3 (EXTop0, ori, beq);
  or or_4 (EXTop1, beq, lui);
  or or_5 (ALUSrc, ori, lw, sw, lui);
  or or_6 (RegDst, ori, lw, lui);
  buf or_7 (MemtoReg, lw);  // OR_Gate
  buf or_8 (nPC_sel, beq);  // OR_Gate
  buf or_9 (ALUop0, sub);  // OR_Gate
  buf or_10 (ALUop1, ori);  // OR_Gate
  buf or_11 (ALUop2, beq);  // OR_Gate
  or or_12 (EXTuse, ori, lw, sw, beq, lui);
endmodule
